# Fritzing sketch OLIXIE (saved by Fritzing 0.9.5d)
breadboards: 2

parts:
  M1 = DOIT Esp32 DevKit v1 (30 pins long, 11 pins width) [part_number=ESP32S-PIN30]
  パーツ1 = Adafruit TCA9548A
  OLED0 = OLED Mono 0.56 inch blue or white
  OLED1 = OLED Mono 0.56 inch blue or white
  OLED3 = OLED Mono 0.56 inch blue or white
  OLED4 = OLED Mono 0.56 inch blue or white
  OLED5 = OLED Mono 0.56 inch blue or white
  OLED6 = OLED Mono 0.56 inch blue or white
  OLED7 = OLED Mono 0.56 inch blue or white
  OLED8 = OLED Mono 0.56 inch blue or white
  Sensor1 = TTP223B Capacitive Touch Sensor Module

nets:
  3V3: M1.3V3, Sensor1.VCC
  GND: M1.GND, パーツ1.GND, OLED0.GND, OLED1.GND, OLED3.GND, OLED4.GND, OLED5.GND, OLED6.GND, OLED7.GND, OLED8.GND, Sensor1.GND
  N1: M1.D2, Sensor1.SIG
  N2: M1.D21, パーツ1.INPUTSDA
  N3: M1.D22, パーツ1.INPUTSCL
  VCC: M1.VIN, パーツ1.VCC, OLED0.VCC, OLED1.VCC, OLED3.VCC, OLED4.VCC, OLED5.VCC, OLED6.VCC, OLED7.VCC, OLED8.VCC
  N4: パーツ1.2SDA, OLED3.SDA
  N5: パーツ1.2SCL, OLED3.SCL
  N6: パーツ1.3SDA, OLED4.SDA
  N7: パーツ1.3SCL, OLED4.SCL
  N8: パーツ1.4SDA, OLED5.SDA
  N9: パーツ1.4SCL, OLED5.SCL
  N10: パーツ1.5SDA, OLED6.SDA
  N11: パーツ1.5SCL, OLED6.SCL
  N12: パーツ1.6SDA, OLED7.SDA
  N13: パーツ1.6SCL, OLED7.SCL
  N14: パーツ1.7SDA, OLED8.SDA
  N15: パーツ1.7SCL, OLED8.SCL
  N16: パーツ1.0SDA, OLED0.SDA
  N17: パーツ1.0SCL, OLED0.SCL
  N18: パーツ1.1SDA, OLED1.SDA
  N19: パーツ1.1SCL, OLED1.SCL

custom parts:
  DOIT Esp32 DevKit v1 (30 pins long, 11 pins width): The DOIT Esp32 DevKit v1 is one of the development board created by DOIT to evaluate the ESP-WROOM-32 module. It is based on the ESP32 microcontroller that boasts Wifi, Bluetooth, Ethernet and Low Power support all in a single chip. (vanepp) made breadboard work, adjusted pin numbering and labels and reduced size of schematic and cleaned up pcb. This chip is 30pins long (2 x15) and 11 pins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
  Adafruit TCA9548A: You just found the perfect I2C sensor, and you want to wire up two or three or more of them to your Arduino when you realize "Uh oh, this chip has a fixed I2C address, and from what I know about I2C, you cannot have two devices with the same address on the same SDA/SCL pins!" Are you out of luck? You would be, if you didn't have this ultra-cool TCA9548A 1-to-8 I2C multiplexer! Finally, a way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
  OLED Mono 0.56 inch blue or white: OLED, I2C 3.3V - 5V Blue and White text versions
  TTP223B Capacitive Touch Sensor Module: The TTP223B capacitive touch sensor module uses the TTP223B IC. The appropriate voltage is approximately 2 to 5.5 volts.
